# Fritzing sketch ESP-PH (saved by Fritzing 0.9.10b)
breadboards: 1

parts:
  M1 = ESP32-S2-DevKitC-1 [part_number=ESP32-S2-DevKitC-1]
  PH4502C = ph-4502c [package=THT]
  DHT11 = Humidity and Temperature Sensor DHT11
  Soil_Moisture_Sensor = Soil Moisture Sensor
  Light_Intensity_Sensor = KY-028 Digital Temperature Sensor Module [package="Breakout board"]

nets:
  N1: M1.pin_1, M1.pin_2
  VCC: M1.pin_21, PH4502C.pin6, DHT11.Vcc, Soil_Moisture_Sensor.VCC, Light_Intensity_Sensor.+
  N2: M1.pin_22, M1.pin_23, M1.pin_24, M1.pin_44, PH4502C.pin4, PH4502C.pin5, DHT11.GND_2, Soil_Moisture_Sensor.GND, Light_Intensity_Sensor.G
  N3: M1.pin_27, PH4502C.pin3
  N4: M1.pin_28, DHT11.Data-signal
  N5: M1.pin_29, Soil_Moisture_Sensor.SIG
  N6: M1.pin_30, Light_Intensity_Sensor.A0

custom parts:
  ESP32-S2-DevKitC-1: ESP32-S2-DevKitC-1 is an entry-level development board based on ESP32-S2-SOLO (on-board PCB antenna). It is based on the ESP32 microcontroller that boasts Wifi, Bluetooth, Ethernet and Low Power support all in a single chip. (vanepp) Feb 2022: converted to ESP32-S2-DevKitC-1. This module is 44pins long (2x22) and 11 pins width.
  ph-4502c: ph-4502c PH Meter.
  Humidity and Temperature Sensor DHT11: Digital relative humidity & temperature sensor DHT11
  KY-028 Digital Temperature Sensor Module: KY-028 Digital Temperature Sensor Module, used to measure changes in temperature.
